# Fritzing sketch electric_circuit (saved by Fritzing 0.9.3b)
breadboards: 1

parts:
  Part1 = FC-28 Soil Hygrometer Module - Probe
  Part2 = FC-28 Soil Hygrometer Module
  Relay_5V1 = Keyes Relay [package=THT]
  U1 = ESP8266 NodeMCU LoLin module
  JACK1 = 2.1mm Barrel Jack with Terminal Block
  Part3 = LCD1602-I2C
  M2 = DC Motor

nets:
  N1: Part1.POS, Part2.POS
  N2: Part1.NEG, Part2.NEG
  VCC: Part2.VCC, Relay_5V1.C, U1.Vin, JACK1.POS, Part3.VCC
  GND: Part2.GND, Relay_5V1.ground, U1.GND, JACK1.NEG, Part3.GND, M2.pin_1
  N3: Part2.AO, U1.A0
  N4: Relay_5V1.signal, U1.D8
  N5: Relay_5V1.power, U1.3V3
  N6: Relay_5V1.NC, M2.pin_2
  N7: U1.D1, Part3.SCL
  N8: U1.D2, Part3.SDA

custom parts:
  FC-28 Soil Hygrometer Module - Probe: The FC-28 is a soil hygrometer module that uses the Texas Instruments LM393 comparator chip to provide an analog measurement of soil humidity.
  FC-28 Soil Hygrometer Module: The FC-28 is a soil hygrometer module that uses the Texas Instruments LM393 comparator chip to provide an analog measurement of soil humidity. The digital output is high when soil moisture is over a certain threshold, as determined by adjusting the potentiometer.
  Keyes Relay: The Keyes 5V relay module is suitable for SCM development, home appliance control. It uses a 5V~12V TIL control signal which can control DC / AC signal.
  ESP8266 NodeMCU LoLin module: ESP8266 based NodeMCU
  LCD1602-I2C: A standard character display, usually with 2x16 characters. Comes in many colors with LCM1602 IIC attached.
